// Logisim project Ип-312 Прохорова Валерия в 48.circ as structural Verilog: 2 circuits, main circuit main
module main (
  output [2:0] r,
  output e,
  output halt
);

  wire and_1_out, clock_1_out, comparator_1_eq, counter_1_carry, not_1_out, or_1_out, Reset_out;
  wire [2:0] rom_1_data;
  wire [3:0] bit_extender_1_out, bit_extender_2_out, bit_extender_3_out, bit_extender_4_out,
       bit_extender_5_out, bit_extender_6_out, counter_1_q;

  Clock clock_1 (.out(clock_1_out));
  not not_1 (not_1_out, counter_1_carry);
  Button Reset (.out(Reset_out));
  and and_1 (and_1_out, clock_1_out, not_1_out);
  or or_1 (or_1_out, and_1_out, e);
  Counter #(.max('hf), .ongoal("stay"), .width(4)) counter_1 (
    .clr(Reset_out), .clk(or_1_out), .carry(counter_1_carry), .Q(counter_1_q));  // open: load, up, count, D
  hw hw_1 (
    .X1(counter_1_q[3]), .X2(counter_1_q[2]), .X3(counter_1_q[1]), .X4(counter_1_q[0]), .F1(r[2]), .F2(r[1]),
    .F3(r[0]));
  ROM #(.addrWidth(4), .dataWidth(3)) rom_1 (.addr(counter_1_q), .data(rom_1_data));
  Hex_Digit_Display F1 (.value(bit_extender_1_out));  // open: dp
  assign bit_extender_1_out = {{3{1'b0}}, r[2]};  // Bit_Extender bit_extender_1
  assign bit_extender_2_out = {{3{1'b0}}, r[1]};  // Bit_Extender bit_extender_2
  assign bit_extender_3_out = {{3{1'b0}}, r[0]};  // Bit_Extender bit_extender_3
  Hex_Digit_Display F2 (.value(bit_extender_2_out));  // open: dp
  Hex_Digit_Display F3 (.value(bit_extender_3_out));  // open: dp
  Comparator #(.width(3)) comparator_1 (.a(r), .b(rom_1_data), .eq(comparator_1_eq));  // open: gt, lt
  not not_2 (e, comparator_1_eq);
  Hex_Digit_Display ExpectedF1 (.value(bit_extender_6_out));  // open: dp
  Hex_Digit_Display ExpectedF2 (.value(bit_extender_5_out));  // open: dp
  Hex_Digit_Display ExpectedF3 (.value(bit_extender_4_out));  // open: dp
  assign bit_extender_4_out = {{3{1'b0}}, rom_1_data[0]};  // Bit_Extender bit_extender_4
  assign bit_extender_5_out = {{3{1'b0}}, rom_1_data[1]};  // Bit_Extender bit_extender_5
  assign bit_extender_6_out = {{3{1'b0}}, rom_1_data[2]};  // Bit_Extender bit_extender_6
  LED ERROR (.in(e));
  LED OK (.in(counter_1_carry));
  or or_2 (halt, e, counter_1_carry);

  // Notes on the sheet:
  //   contents of rom_1 (hex, n*v repeats v):
  //   2 7 1 1 1 2 4 6 7 7 0 2 6 1 5 3
endmodule

module hw (
  input  X1,
  input  X2,
  input  X3,
  input  X4,
  output F1,
  output F2,
  output F3
);

  wire and_1_out, and_2_out, and_3_out, and_4_out, and_5_out, and_6_out, and_7_out, and_8_out, and_9_out,
       and_10_out, and_11_out, and_12_out, and_13_out, and_14_out, not_1_out, not_2_out, not_3_out, not_4_out;

  not not_1 (not_1_out, X1);
  not not_2 (not_2_out, X2);
  not not_3 (not_3_out, X3);
  not not_4 (not_4_out, X4);
  and and_1 (and_1_out, not_2_out, not_3_out, X4);
  and and_2 (and_2_out, not_1_out, X2, X3);
  and and_3 (and_3_out, X1, not_3_out, not_4_out);
  and and_4 (and_4_out, X1, X2, not_4_out);
  and and_5 (and_5_out, not_2_out, not_3_out);
  and and_6 (and_6_out, not_1_out, X2, X4);
  and and_7 (and_7_out, X1, not_3_out, not_4_out);
  and and_8 (and_8_out, X1, X3, X4);
  and and_9 (and_9_out, not_1_out, not_2_out, X4);
  and and_10 (and_10_out, not_1_out, not_2_out, X3);
  and and_11 (and_11_out, not_1_out, X2, not_3_out, not_4_out);
  and and_12 (and_12_out, X1, not_2_out, not_3_out);
  and and_13 (and_13_out, X1, not_3_out, X4);
  and and_14 (and_14_out, X1, X2, X3);
  or or_1 (F1, and_1_out, and_2_out, and_3_out, and_4_out);
  or or_2 (F2, and_5_out, and_6_out, and_7_out, and_8_out);
  or or_3 (F3, and_9_out, and_10_out, and_11_out, and_12_out, and_13_out, and_14_out);
endmodule
